// Logisim project Assignment-1, Task 1.circ as structural Verilog: 2 circuits, main circuit main
module main (
  input  A,
  input  A_2,
  input  A_3,
  input  A_4,
  input  B,
  input  B_2,
  input  A_5,
  input  A_6,
  input  B_3,
  input  B_4,
  output A_A__prime_A_prime,
  output A_prime,
  output A_B,
  output AB,
  output A_B_2,
  output AB_2
);

  wire nand_2_out, nand_3_out, nand_4_out, nor_2_out, nor_3_out, nor_4_out;

  nand nand_1 (A_A__prime_A_prime, A, A);
  nand nand_2 (nand_2_out, A_4, B_2);
  nand nand_3 (nand_3_out, A_5, A_5);
  nand nand_4 (nand_4_out, B_3, B_3);
  nand nand_5 (AB, nand_2_out, nand_2_out);
  nand nand_6 (A_B_2, nand_3_out, nand_4_out);
  nor nor_1 (A_prime, A_2, A_2);
  nor nor_2 (nor_2_out, A_3, B);
  nor nor_3 (nor_3_out, A_6, A_6);
  nor nor_4 (nor_4_out, B_4, B_4);
  nor nor_5 (A_B, nor_2_out, nor_2_out);
  nor nor_6 (AB_2, nor_3_out, nor_4_out);

  // Notes on the sheet:
  //   Implementing NOT gate using NAND gate
  //   Implementing AND gate using NAND gate
  //   Implementing OR gate using NAND gate
  //   (AB)'
  //   A'
  //   B'
  //   Implementing NOT gate using NOR gate
  //   Implementing OR gate using NOR gate
  //   Implementing AND gate using NOR gate
  //   (A+B)'
  //   (A+B)'
  //   (A+A)'
  //   (B+B)'
endmodule

module Task_1 (
  input  A,
  input  A_2,
  input  A_3,
  input  A_4,
  input  B,
  input  B_2,
  input  A_5,
  input  A_6,
  input  B_3,
  input  B_4,
  output A_A__prime_A_prime,
  output A_prime,
  output A_B,
  output AB,
  output A_B_2,
  output AB_2
);

  wire nand_2_out, nand_3_out, nand_4_out, nor_2_out, nor_3_out, nor_4_out;

  nand nand_1 (A_A__prime_A_prime, A, A);
  nand nand_2 (nand_2_out, A_4, B_2);
  nand nand_3 (nand_3_out, A_5, A_5);
  nand nand_4 (nand_4_out, B_3, B_3);
  nand nand_5 (AB, nand_2_out, nand_2_out);
  nand nand_6 (A_B_2, nand_3_out, nand_4_out);
  nor nor_1 (A_prime, A_2, A_2);
  nor nor_2 (nor_2_out, A_3, B);
  nor nor_3 (nor_3_out, A_6, A_6);
  nor nor_4 (nor_4_out, B_4, B_4);
  nor nor_5 (A_B, nor_2_out, nor_2_out);
  nor nor_6 (AB_2, nor_3_out, nor_4_out);

  // Notes on the sheet:
  //   Implementing NOT gate using NAND gate
  //   Implementing AND gate using NAND gate
  //   Implementing OR gate using NAND gate
  //   (AB)'
  //   A'
  //   B'
  //   Implementing NOT gate using NOR gate
  //   Implementing OR gate using NOR gate
  //   Implementing AND gate using NOR gate
  //   (A+B)'
  //   (A+B)'
  //   (A+A)'
  //   (B+B)'
endmodule
