// Logisim project Assignment-1,Task 2.circ as structural Verilog: 2 circuits, main circuit main
module main (
  input  A,
  input  B,
  input  A_2,
  input  A_3,
  input  B_2,
  input  A_4,
  input  B_3,
  input  A_5,
  input  B_4,
  input  A_6,
  input  B_5,
  input  A_7,
  input  B_6,
  output out_14,
  output A_prime,
  output AB,
  output out_17,
  output A_B,
  output AB_A_prime_B_prime,
  output AB_A_prime_B_prime_2
);

  wire nand_1_out, nand_2_out, nand_3_out, nand_4_out, nand_5_out, nand_6_out, nand_8_out, nor_1_out,
       nor_2_out, nor_3_out, nor_4_out, nor_5_out, nor_6_out, nor_7_out, nor_11_out, nor_12_out, nor_13_out;

  nand nand_1 (nand_1_out, A, B);
  nor nor_1 (nor_1_out, A_3, A_3);
  nor nor_2 (nor_2_out, B_2, B_2);
  nor nor_3 (nor_3_out, B_2, A_3);
  nand nand_2 (nand_2_out, A_6, B_5);
  nor nor_4 (nor_4_out, A_7, B_6);
  nand nand_3 (nand_3_out, A, nand_1_out);
  nand nand_4 (nand_4_out, nand_1_out, A);
  nor nor_5 (nor_5_out, nor_1_out, nor_2_out);
  nand nand_5 (nand_5_out, A_6, nand_2_out);
  nand nand_6 (nand_6_out, nand_2_out, A_6);
  nor nor_6 (nor_6_out, A_7, nor_4_out);
  nor nor_7 (nor_7_out, nor_4_out, A_7);
  nand nand_7 (out_14, nand_3_out, nand_4_out);
  nor nor_8 (out_17, nor_5_out, nor_3_out);
  nand nand_8 (nand_8_out, nand_5_out, nand_6_out);
  nor nor_9 (AB_A_prime_B_prime_2, nor_6_out, nor_7_out);
  nand nand_9 (AB_A_prime_B_prime, nand_8_out, nand_8_out);
  nor nor_10 (A_prime, A_2, A_2);
  nor nor_11 (nor_11_out, A_4, A_4);
  nor nor_12 (nor_12_out, B_3, B_3);
  nor nor_13 (nor_13_out, A_5, B_4);
  nor nor_14 (AB, nor_11_out, nor_12_out);
  nor nor_15 (A_B, nor_13_out, nor_13_out);

  // Notes on the sheet:
  //   Implementing XOR gate using NAND gate
  //   Implementing XOR gate using NOR gate
  //   Implementing XNOR gate using NAND gate
  //   Implementing XNOR gate using NOR gate
  //   (AB)'
  //   A'
  //   B'
  //   (AB)'
  //   (A+B)'
  //   (A+B)'
  //   (A(AB)')' = A' + (AB)
  //   (B+(AB)')' =B'+AB
  //   (A'+B')' = AB
  //   (A(AB)')'
  //   (B(AB)')'
  //   (A+(A+B)')'
  //   (B+(A+B)')'
  //   (AB+(A+B)')' = A'b = B'A
  //   ((A'+AB)(B'=AB))'
  //   Implementing NOT gate using NOR gate
  //   Implementing AND gate using NOR gate
  //   Implementing OR gate using NOR gate
  //   (A+A)'
  //   (B+B)'
  //             (A+B)'
  //   (A+B)'
endmodule

module Task2 (
  input  A,
  input  B,
  input  A_2,
  input  A_3,
  input  B_2,
  input  A_4,
  input  B_3,
  input  A_5,
  input  B_4,
  input  A_6,
  input  B_5,
  input  A_7,
  input  B_6,
  output out_14,
  output A_prime,
  output AB,
  output out_17,
  output A_B,
  output AB_A_prime_B_prime,
  output AB_A_prime_B_prime_2
);

  wire nand_1_out, nand_2_out, nand_3_out, nand_4_out, nand_5_out, nand_6_out, nand_8_out, nor_1_out,
       nor_2_out, nor_3_out, nor_4_out, nor_5_out, nor_6_out, nor_7_out, nor_11_out, nor_12_out, nor_13_out;

  nand nand_1 (nand_1_out, A, B);
  nor nor_1 (nor_1_out, A_3, A_3);
  nor nor_2 (nor_2_out, B_2, B_2);
  nor nor_3 (nor_3_out, B_2, A_3);
  nand nand_2 (nand_2_out, A_6, B_5);
  nor nor_4 (nor_4_out, A_7, B_6);
  nor nor_5 (nor_5_out, nor_1_out, nor_2_out);
  nand nand_3 (nand_3_out, A_6, nand_2_out);
  nand nand_4 (nand_4_out, nand_2_out, A_6);
  nor nor_6 (nor_6_out, A_7, nor_4_out);
  nor nor_7 (nor_7_out, nor_4_out, A_7);
  nand nand_5 (nand_5_out, A, nand_1_out);
  nand nand_6 (nand_6_out, nand_1_out, A);
  nand nand_7 (out_14, nand_5_out, nand_6_out);
  nor nor_8 (out_17, nor_5_out, nor_3_out);
  nand nand_8 (nand_8_out, nand_3_out, nand_4_out);
  nor nor_9 (AB_A_prime_B_prime_2, nor_6_out, nor_7_out);
  nand nand_9 (AB_A_prime_B_prime, nand_8_out, nand_8_out);
  nor nor_10 (A_prime, A_2, A_2);
  nor nor_11 (nor_11_out, A_4, A_4);
  nor nor_12 (nor_12_out, B_3, B_3);
  nor nor_13 (nor_13_out, A_5, B_4);
  nor nor_14 (AB, nor_11_out, nor_12_out);
  nor nor_15 (A_B, nor_13_out, nor_13_out);

  // Notes on the sheet:
  //   Implementing XOR gate using NAND gate
  //   Implementing XOR gate using NOR gate
  //   Implementing XNOR gate using NAND gate
  //   Implementing XNOR gate using NOR gate
  //   (AB)'
  //   A'
  //   B'
  //   (A+B)'
  //   (AB)'
  //   (A+B)'
  //   (A'+B')' = AB
  //   (B(AB)')'
  //   (A(AB)')' = A' + (AB)
  //   (B+(AB)')' =B'+AB
  //   (A(AB)')'
  //   (A+(A+B)')'
  //   (B+(A+B)')'
  //   (AB+(A+B)')' = A'b = B'A
  //   ((A'+AB)(B'=AB))'
  //   Implementing NOT gate using NOR gate
  //   Implementing AND gate using NOR gate
  //   Implementing OR gate using NOR gate
  //   (A+A)'
  //   (B+B)'
  //   (A+B)'
  //             (A+B)'
endmodule
