// Logisim project Assignment-1,Task 3 NAND gate.circ as structural Verilog: 2 circuits, main circuit main
module main (
  input  A,
  input  B,
  input  C,
  output AC_BC_prime
);

  wire n7400_1_out_9, n7400_1_out_10, n7400_1_out_11, n7400_1_out_12, n7400_2_out_9;

  _7400 u_7400_1 (
    .in_1(C), .in_2(A), .in_3(n7400_1_out_9), .in_4(n7400_1_out_9), .in_5(n7400_1_out_10),
    .in_6(n7400_1_out_10), .in_7(C), .in_8(C), .out_9(n7400_1_out_9), .out_10(n7400_1_out_10),
    .out_11(n7400_1_out_11), .out_12(n7400_1_out_12));
  _7400 u_7400_2 (
    .in_1(n7400_1_out_12), .in_2(B), .in_7(n7400_1_out_11), .in_8(n7400_2_out_9), .out_9(n7400_2_out_9),
    .out_12(AC_BC_prime));  // open: in_3, in_4, in_5, in_6, out_10, out_11

  // Notes on the sheet:
  //   C
  //   C
  //   A
  //   AC
  //   B
  //   C'
  //   (AC)'
  //   (BC')'
endmodule

module _7400 (
  input  in_1,
  input  in_2,
  input  in_3,
  input  in_4,
  input  in_5,
  input  in_6,
  input  in_7,
  input  in_8,
  output out_9,
  output out_10,
  output out_11,
  output out_12
);

  nand nand_1 (out_9, in_1, in_2);
  nand nand_2 (out_10, in_3, in_4);
  nand nand_3 (out_11, in_5, in_6);
  nand nand_4 (out_12, in_7, in_8);
endmodule
