// Logisim project Assignment 3 c.circ as structural Verilog: 4 circuits, main circuit main
module main (
  input  W,
  input  X,
  input  Y,
  input  Z,
  output A___W___XZ___XY,
  output out_6,
  output out_7,
  output out_8
);

  wire n7404_1_out_7, n7404_1_out_8, n7404_1_out_9, n7408_1_out_9, n7408_1_out_10, n7408_1_out_11,
       n7408_1_out_12, n7408_2_out_9, n7408_2_out_10, n7408_2_out_11, n7408_2_out_12, n7432_1_out_10,
       n7432_1_out_12;

  _7404 u_7404_1 (
    .in_1(Y), .in_2(X), .in_3(W), .in_4(Z), .out_7(n7404_1_out_7), .out_8(n7404_1_out_8),
    .out_9(n7404_1_out_9), .out_10(out_8));  // open: in_5, in_6, out_11, out_12
  _7408 u_7408_1 (
    .in_1(Y), .in_2(X), .in_3(Z), .in_4(X), .in_5(Y), .in_6(n7404_1_out_8), .in_7(Z), .in_8(n7404_1_out_8),
    .out_9(n7408_1_out_9), .out_10(n7408_1_out_10), .out_11(n7408_1_out_11), .out_12(n7408_1_out_12));
  _7408 u_7408_2 (
    .in_1(out_8), .in_2(n7408_2_out_10), .in_3(n7404_1_out_7), .in_4(X), .in_5(Z), .in_6(Y), .in_7(out_8),
    .in_8(n7404_1_out_7), .out_9(n7408_2_out_9), .out_10(n7408_2_out_10), .out_11(n7408_2_out_11),
    .out_12(n7408_2_out_12));
  _7432 u_7432_1 (
    .in_1(W), .in_2(n7432_1_out_10), .in_3(n7408_1_out_9), .in_4(n7408_1_out_10), .in_5(n7432_1_out_12),
    .in_6(n7408_1_out_12), .in_7(n7408_1_out_11), .in_8(n7408_2_out_9), .out_9(A___W___XZ___XY),
    .out_10(n7432_1_out_10), .out_11(out_6), .out_12(n7432_1_out_12));
  _7432 u_7432_2 (
    .in_1(n7408_2_out_11), .in_2(n7408_2_out_12), .out_9(out_7));  // open: in_3, in_4, in_5, in_6, in_7, in_8, out_10, out_11, out_12

  // Notes on the sheet:
  //   W'
  //   X'
  //   Y'
  //   Z'
  //   B = X'Z + X'Y + XY'Z'
  //   C = Y'Z' + YZ
  //   D = Z'
endmodule

module _7404 (
  input  in_1,
  input  in_2,
  input  in_3,
  input  in_4,
  input  in_5,
  input  in_6,
  output out_7,
  output out_8,
  output out_9,
  output out_10,
  output out_11,
  output out_12
);

  not not_1 (out_7, in_1);
  not not_2 (out_8, in_2);
  not not_3 (out_9, in_3);
  not not_4 (out_10, in_4);
  not not_5 (out_11, in_5);
  not not_6 (out_12, in_6);
endmodule

module _7432 (
  input  in_1,
  input  in_2,
  input  in_3,
  input  in_4,
  input  in_5,
  input  in_6,
  input  in_7,
  input  in_8,
  output out_9,
  output out_10,
  output out_11,
  output out_12
);

  or or_1 (out_9, in_1, in_2);
  or or_2 (out_10, in_3, in_4);
  or or_3 (out_11, in_5, in_6);
  or or_4 (out_12, in_7, in_8);
endmodule

module _7408 (
  input  in_1,
  input  in_2,
  input  in_3,
  input  in_4,
  input  in_5,
  input  in_6,
  input  in_7,
  input  in_8,
  output out_9,
  output out_10,
  output out_11,
  output out_12
);

  and and_1 (out_9, in_1, in_2);
  and and_2 (out_10, in_3, in_4);
  and and_3 (out_11, in_5, in_6);
  and and_4 (out_12, in_7, in_8);
endmodule
