// Logisim project Assignment 6 Task 1 D1.circ as structural Verilog: 1 circuit, main circuit main
module main (
  input  E,
  input  I0,
  input  I1,
  input  I2,
  input  I3,
  input  S1,
  input  S2,
  output out_8
);

  wire and_1_out, and_2_out, and_3_out, and_4_out, not_1_out, not_2_out;

  not not_1 (not_1_out, S2);
  not not_2 (not_2_out, S1);
  and and_1 (and_1_out, I0, not_2_out, not_1_out, E);
  and and_2 (and_2_out, I1, not_2_out, S2, E);
  and and_3 (and_3_out, I2, S1, not_1_out, E);
  and and_4 (and_4_out, I3, S1, S2, E);
  or or_1 (out_8, and_1_out, and_2_out, and_3_out, and_4_out);
endmodule
