// Logisim project Week 9 Assignment.circ as structural Verilog: 1 circuit, main circuit main
module main (
  input  A,
  output out_2,
  output out_3
);

  wire clock_1_out, DB_qn, xor_1_out, xor_2_out;

  xor xor_1 (xor_1_out, out_2, out_3);
  xor xor_2 (xor_2_out, xor_1_out, A);
  D_Flip_Flop DA (.clk(clock_1_out), .D(xor_2_out), .Q(out_2));  // open: Qn, preset, en, reset
  D_Flip_Flop DB (.clk(clock_1_out), .D(DB_qn), .Q(out_3), .Qn(DB_qn));  // open: preset, en, reset
  Clock clock_1 (.out(clock_1_out));

  // Notes on the sheet:
  //   B
endmodule
